# Fritzing sketch AOM_IoT_Bit_V2.0 (saved by Fritzing 0.9.9b)
breadboards: 1

parts:
  MKR_1010 = Arduino MKR Wifi 1010
  Post_Switch = Toggle Switch [package=THT]
  Get_Switch = Toggle Switch [package=THT]
  Post_LED = LED - 5mm [color="Red (633nm)" current=0.030 package="5 mm [THT]"]
  Get_LED = LED - 5mm [color="Red (633nm)" current=0.030 package="5 mm [THT]"]
  Post_LED_Res = Resistor [tolerance=±5% resistance=100 power=0.25 package=THT]
  Get_LED_Res = Resistor [tolerance=±5% resistance=100 power=0.25 package=THT]
  Conn_LED = LED - 5mm [color="Blue (525nm)" current=0.030 package="5 mm [THT]"]
  Conn_LED_Res = Resistor [tolerance=±5% resistance=10k power=0.25 package=THT]
  3_=_collector_2_=_emitter_Current_goes_from_collector_to_emitter = PNP-Transistor [package="TO92 [THT]"]
  Output = LITTLEBITS_MALE [package=little_bits_male]
  R1 = Resistor [tolerance=±5% power=0.25 resistance=220 package=THT]
  Input = LITTLEBITS_FEMALE [package=little_bits_female]
  R2 = Resistor [tolerance=±5% power=0.25 resistance=220 package=THT]

nets:
  GND: MKR_1010.GND, Post_Switch.L1, Get_Switch.L1, Post_LED.cathode, Get_LED.cathode, Conn_LED.cathode, Output.GND, Input.GND
  N1: MKR_1010.A1, Conn_LED_Res.Pin_0
  N2: MKR_1010.A2, Post_LED_Res.Pin_0
  N3: MKR_1010.A3, Post_Switch.COM
  N4: MKR_1010.A5, R2.Pin_0
  N5: MKR_1010.A6, R1.Pin_0
  N6: MKR_1010.D0, Get_LED_Res.Pin_0
  N7: MKR_1010.D1, Get_Switch.COM
  N8: MKR_1010.+3V3, Post_Switch.L2, Get_Switch.L2
  VIN: MKR_1010.VIN, Input.VCC
  +5V: MKR_1010.+5V, 3_=_collector_2_=_emitter_Current_goes_from_collector_to_emitter.C, Output.VCC
  N9: Post_LED.anode, Post_LED_Res.Pin_1
  N10: Get_LED.anode, Get_LED_Res.Pin_1
  N11: Conn_LED.anode, Conn_LED_Res.Pin_1
  N12: 3_=_collector_2_=_emitter_Current_goes_from_collector_to_emitter.E, Output.SIG
  N13: 3_=_collector_2_=_emitter_Current_goes_from_collector_to_emitter.B, R1.Pin_1
  N14: Input.SIG, R2.Pin_1

custom parts:
  Arduino MKR Wifi 1010: Arduino MKR Wifi 1010, SAMD21 Cortex-M0+ 32bit Low Power ARM MCU,Flash Memory 256 KB, SRAM 32KB, 48mhz clock, Ublok Wifi interface.
